# Fritzing sketch monk-circuit (saved by Fritzing 0.9.3b)
breadboards: 1

parts:
  P1 = POT [package=pot_mammoth]
  P2 = POT [package=pot_mammoth]
  P3 = POT [package=pot_mammoth]
  P5 = POT [package=pot_mammoth]
  P6 = POT [package=pot_mammoth]
  P4 = POT [package=pot_mammoth]
  Arduino = Arduino Uno (Rev3) - ICSP

nets:
  N1: P1.S, P2.S, P3.S, P5.S, P6.S, P4.S, Arduino.GND
  N2: P1.A, Arduino.A0
  N3: P1.E, P2.E, P3.E, P5.E, P6.E, P4.E, Arduino.5V
  N4: P2.A, Arduino.A1
  N5: P3.A, Arduino.A2
  N6: P5.A, Arduino.A4/SDA
  N7: P6.A, Arduino.A5/SCL
  N8: P4.A, Arduino.A3

notes:
  Arduino Uno
  USB connection sends the readings of the six Potentiometers to the computer. The PureData patch will collect those readings and utilize them to produce some sound.
  The Potentiometers' connection to the Arduino is pretty straightforward.
  It can be set up on a breadboard in about 5 minutes.
  MONK Programmable Digital Synthesizer: Hardware Diagram
  made by Kostas Sfikas,
  April 2017
